# Fritzing sketch Charduino (saved by Fritzing 0.9.4)
circuit board: 8.14067cm x 6.92031cm
breadboards: 1

parts:
  Charduino = Arduino Nano (Rev3.0)
  R1 = Resistor [tolerance=±5% resistance=2.2k package=THT]
  C1 = Electrolytic Capacitor [capacitance=22µF voltage=50V package="100 mil [THT, electrolytic]"]
  PWM_gachette = female pin header, 3 pins [form="♀ (female)"]
  Diode = female pin header, 3 pins [form="♀ (female)"]
  Contrôleur_activation = female pin header, 2 pins [form="♀ (female)"]
  NPN = NPN-Transistor [package="TO92 [THT]"]
  R3 = Resistor [tolerance=±5% resistance=2.2k package=THT]
  Frein_moteur_CTRL = female pin header, 2 pins [form="♀ (female)"]
  R4 = Resistor [tolerance=±5% resistance=2.2k package=THT]
  R6 = Resistor [tolerance=±5% resistance=2.2k package=THT]
  Wattmètre = female pin header, 4 pins [form="♀ (female)"]
  Panneau_contrôle = female pin header, 4 pins [form="♀ (female)"]
  HX711 = HX711 Weighing Sensor Module
  Capteur_de_force = female pin header, 4 pins [form="♀ (female)"]
  Interrupteurs = female pin header, 4 pins [form="♀ (female)"]
  Hall = female pin header, 3 pins [form="♀ (female)"]
  GV5-1 = Omron_MY2K_02_12VDC_3A [part_number=GV5-2 package=THT]
  GND_interrupteurs = female pin header, 7 pins [form="♀ (female)"]
  U1 = Buck regulator LM7525 [part_number=LM2575 package=TO-263]  # not connected
  D1 = Schottky Diode [part_number=1N5817 package="300 mil [THT]"]
  Batterie = rounded female pin header, 2 pins [form="♀ (female rounded)"]
  Capa_alim_Vin = Electrolytic Capacitor [capacitance=10µ voltage=50V part_number="100 µF" package="100 mil [THT, electrolytic]"]
  Capa_alim_Vout = Electrolytic Capacitor [capacitance=0.1mF voltage=10V part_number="330 µF" package="100 mil [THT, electrolytic]"]
  L2 = Inductor [inductance=330µH package="400 mil [THT]"]
  IC1 = LM2575 [package=to-220-alt]

nets:
  GND: Charduino.GND, C1.-, PWM_gachette.pin3, Diode.pin2, R4.Pin_1, R6.Pin_0, Wattmètre.pin1, Panneau_contrôle.pin1, HX711.GND, Hall.pin1, GV5-1.Set/Reset#89, GND_interrupteurs.pin1, GND_interrupteurs.pin2, GND_interrupteurs.pin3, GND_interrupteurs.pin4, GND_interrupteurs.pin5, GND_interrupteurs.pin6, GND_interrupteurs.pin7, D1.anode, Batterie.pin2, Capa_alim_Vin.-, Capa_alim_Vout.-, IC1.Gnd
  N1: Charduino.D2, Interrupteurs.pin4
  N2: Charduino.D3, Interrupteurs.pin3
  N3: Charduino.D4, Interrupteurs.pin2
  N4: Charduino.D5, Interrupteurs.pin1
  N5: Charduino.D6, R1.Pin_0
  N6: Charduino.D7, HX711.DO/RX
  N7: Charduino.D8, HX711.CK/TX
  N8: Charduino.D9, Diode.pin3
  N9: Charduino.D10, R3.Pin_0
  N10: Charduino.D12/MISO, PWM_gachette.pin1, R4.Pin_0
  VIN: Charduino.VIN, Diode.pin1, Wattmètre.pin4, HX711.VCC, Capa_alim_Vout.+, L2.pin_1, IC1.Feedback
  N11: Charduino.A7, Wattmètre.pin3
  N12: Charduino.A6, Wattmètre.pin2
  N13: Charduino.A5, Panneau_contrôle.pin4
  N14: Charduino.A4, Panneau_contrôle.pin3
  N15: Charduino.A3, Panneau_contrôle.pin2
  N16: Charduino.A1, Hall.pin3
  N17: Charduino.A0, Hall.pin2
  N18: Charduino.D13/SCK, R6.Pin_1, GV5-1.Set/Reset#90
  N19: R1.Pin_1, C1.+, PWM_gachette.pin2
  N20: Contrôleur_activation.pin1, GV5-1.Out_1-2
  N21: Contrôleur_activation.pin2, GV5-1.Vcc/GND
  N22: NPN.E, Frein_moteur_CTRL.pin2
  N23: NPN.B, R3.Pin_1
  N24: NPN.C, Frein_moteur_CTRL.pin1
  N25: HX711.E+, Capteur_de_force.pin4
  N26: HX711.E-, Capteur_de_force.pin3
  N27: HX711.A+, Capteur_de_force.pin2
  N28: HX711.A-, Capteur_de_force.pin1
  N29: D1.cathode, L2.pin_0, IC1.Output
  N30: Batterie.pin1, Capa_alim_Vin.+, IC1.Vin

custom parts:
  Omron_MY2K_02_12VDC_3A: Omron GV5-2, 12VDC @ 2 Amp, Bistable, Low Signal Relay, DPDT, No Coil Polarity
  Buck regulator LM7525: 5V DC Voltage Regulator - LM2575 LM2576
