# Fritzing sketch Wattmetre (saved by Fritzing 0.9.2b)
breadboards: 1

parts:
  Composant1 = Arduino Nano (Rev3.0)
  R1 = Resistor [tolerance=±5% resistance=10k package=THT]
  R1_2 = Resistor [tolerance=±5% resistance=10k package=THT]
  R2 = Resistor [tolerance=±5% resistance=470k package=THT]
  R2_2 = Resistor [tolerance=±5% resistance=470k package=THT]
  R_shunt = Resistor [tolerance=±5% resistance=5m package=THT]
  U2 = LM 358 Dual Op-Amp [package="DIP8 [THT]"]
  Controleur_Ozo = female pin header, 2 pins [form="♀ (female)"]
  Batterie_42V = Battery block 9V
  Ru1 = Resistor [tolerance=±5% resistance=10k package=THT]
  Ru2 = Resistor [tolerance=±20% resistance=1k package=THT]
  C1 = Electrolytic Capacitor [capacitance=1µF package="100 mil [THT, electrolytic]"]
  R3 = Resistor [tolerance=±5% resistance=39k package=THT]

nets:
  GND: Composant1.GND, R1_2.Pin_1, R_shunt.Pin_1, U2.connector3, Batterie_42V.+, Ru2.Pin_0, C1.-, R3.Pin_0
  N1: Composant1.5V, U2.connector7
  N2: Composant1.A5, Ru1.Pin_0, Ru2.Pin_1, R3.Pin_1
  N3: Composant1.A4, R2.Pin_1, U2.connector0, C1.+
  N4: R1.Pin_0, R2_2.Pin_1, U2.connector2
  N5: R1.Pin_1, R_shunt.Pin_0, Controleur_Ozo.pin1
  N6: R1_2.Pin_0, R2.Pin_0, U2.connector1
  N7: Controleur_Ozo.pin2, Batterie_42V.-, Ru1.Pin_1
