# Fritzing sketch PID_Basic (saved by Fritzing 0.9.2b)
breadboards: 1

parts:
  Composant1 = Arduino Nano (Rev3.0)
  R1 = Resistor [tolerance=±5% resistance=3.3k package=THT]
  C1 = Electrolytic Capacitor [capacitance=10µF voltage=50V package="100 mil [THT, electrolytic]"]
  PWM_gachette = female pin header, 3 pins [form="♀ (female)"]
  S1 = Pushbutton [package=THT]
  S2 = Pushbutton [package=THT]
  S3 = Pushbutton [package=THT]
  VCC_GND_Hall = female pin header, 2 pins [form="♀ (female)"]
  Hall = female pin header, 3 pins [form="♀ (female)"]
  C2 = Ceramic Capacitor [capacitance=100nF package="100 mil [THT, multilayer]"]
  C3 = Ceramic Capacitor [capacitance=100nF package="100 mil [THT, multilayer]"]
  Diode = female pin header, 3 pins [form="♀ (female)"]
  HX711_Data = female pin header, 2 pins [form="♀ (female)"]
  frein_inertie = Pushbutton [package=THT]
  Ozo_+- = female pin header, 2 pins [form="♀ (female)"]
  NPN = NPN-Transistor [package="TO92 [THT]"]
  R3 = Resistor [tolerance=±5% resistance=2.2k package=THT]
  Frein_moteur_CTRL = female pin header, 2 pins [form="♀ (female)"]
  R4 = Resistor [tolerance=±5% resistance=2.2k package=THT]
  U1 = RELAY [package=relay-jzc]
  Batterie = female pin header, 2 pins [form="♀ (female)"]
  Q1 = MOSFET-NCHANNEL [package=to220v]
  R5 = Resistor [tolerance=±5% resistance=2.2k package=THT]
  R6 = Resistor [tolerance=±5% resistance=2.2k package=THT]
  Wattmètre = female pin header, 4 pins [form="♀ (female)"]
  HX711_VCC_GND = female pin header, 2 pins [form="♀ (female)"]

nets:
  GND: Composant1.GND, C1.-, PWM_gachette.pin3, S1.leg1, S2.leg1, S3.leg1, VCC_GND_Hall.pin1, Diode.pin2, frein_inertie.leg1, R4.Pin_1, Batterie.pin2, Q1.S, R6.Pin_0, Wattmètre.pin4, HX711_VCC_GND.pin2
  N1: Composant1.D2, frein_inertie.leg0
  N2: Composant1.D3, S1.leg0
  N3: Composant1.D4, S2.leg0
  N4: Composant1.D5, S3.leg0
  N5: Composant1.D6, R1.Pin_0
  N6: Composant1.D7, HX711_Data.pin2
  N7: Composant1.D8, HX711_Data.pin1
  N8: Composant1.D9, Diode.pin3
  N9: Composant1.D10, R3.Pin_0
  N10: Composant1.D12/MISO, PWM_gachette.pin1, R4.Pin_0
  N11: Composant1.VIN, Diode.pin1, HX711_VCC_GND.pin1
  N12: Composant1.A5, Wattmètre.pin3
  N13: Composant1.A4, Wattmètre.pin2
  N14: Composant1.A1, Hall.pin2, C2.0
  N15: Composant1.A0, Hall.pin1, C3.0
  N16: Composant1.D13/SCK, Q1.G, R6.Pin_1
  N17: R1.Pin_1, C1.+, PWM_gachette.pin2
  N18: VCC_GND_Hall.pin2, C2.1, C3.1
  N19: Ozo_+-.pin1, U1.MAIN
  N20: Ozo_+-.pin2, U1.NO
  N21: NPN.E, Frein_moteur_CTRL.pin2
  N22: NPN.B, R3.Pin_1
  N23: NPN.C, Frein_moteur_CTRL.pin1
  N24: U1.COIL2, Q1.D
  N25: U1.COIL1, R5.Pin_1
  N26: Batterie.pin1, R5.Pin_0
